// Logisim project ProcesadorMonociclo_registros.circ as structural Verilog
module BR (
  input  [15:0] DATA
);

  wire clock_1_out, decoder_1_out0, decoder_1_out1, decoder_1_out2, decoder_1_out3, decoder_1_out4,
       decoder_1_out5, decoder_1_out6, decoder_1_out7, decoder_1_out8, decoder_1_out9, decoder_1_out10,
       decoder_1_out11, decoder_1_out12, decoder_1_out13, decoder_1_out14, decoder_1_out15;
  wire [15:0] and_1_out;

  Decoder #(.select(4)) decoder_1 (
    .out0(decoder_1_out0), .out1(decoder_1_out1), .out2(decoder_1_out2), .out3(decoder_1_out3),
    .out4(decoder_1_out4), .out5(decoder_1_out5), .out6(decoder_1_out6), .out7(decoder_1_out7),
    .out8(decoder_1_out8), .out9(decoder_1_out9), .out10(decoder_1_out10), .out11(decoder_1_out11),
    .out12(decoder_1_out12), .out13(decoder_1_out13), .out14(decoder_1_out14), .out15(decoder_1_out15));  // open: sel, en
  Clock clock_1 (.out(clock_1_out));
  assign and_1_out = {16{1'b0}} & DATA;  // AND_Gate and_1, 16 bits wide
  Register #(.width(16)) r0 (.D(and_1_out), .en(decoder_1_out0), .clk(clock_1_out));  // open: Q, clr
  Register #(.width(16)) register_1 (.D(DATA), .en(decoder_1_out1), .clk(clock_1_out));  // open: Q, clr
  Register #(.width(16)) r2 (.D(DATA), .en(decoder_1_out2), .clk(clock_1_out));  // open: Q, clr
  Register #(.width(16)) r3 (.D(DATA), .en(decoder_1_out3), .clk(clock_1_out));  // open: Q, clr
  Register #(.width(16)) r4 (.D(DATA), .en(decoder_1_out4), .clk(clock_1_out));  // open: Q, clr
  Register #(.width(16)) register_2 (.D(DATA), .en(decoder_1_out5), .clk(clock_1_out));  // open: Q, clr
  Register #(.width(16)) r6 (.D(DATA), .en(decoder_1_out6), .clk(clock_1_out));  // open: Q, clr
  Register #(.width(16)) r7 (.D(DATA), .en(decoder_1_out7), .clk(clock_1_out));  // open: Q, clr
  Register #(.width(16)) r8 (.D(DATA), .en(decoder_1_out8), .clk(clock_1_out));  // open: Q, clr
  Register #(.width(16)) r9 (.D(DATA), .en(decoder_1_out9), .clk(clock_1_out));  // open: Q, clr
  Register #(.width(16)) r10 (.D(DATA), .en(decoder_1_out10), .clk(clock_1_out));  // open: Q, clr
  Register #(.width(16)) register_3 (.D(DATA), .en(decoder_1_out11), .clk(clock_1_out));  // open: Q, clr
  Register #(.width(16)) r12 (.D(DATA), .en(decoder_1_out12), .clk(clock_1_out));  // open: Q, clr
  Register #(.width(16)) r13 (.D(DATA), .en(decoder_1_out13), .clk(clock_1_out));  // open: Q, clr
  Register #(.width(16)) r14 (.D(DATA), .en(decoder_1_out14), .clk(clock_1_out));  // open: Q, clr
  Register #(.width(16)) r15 (.D(DATA), .en(decoder_1_out15), .clk(clock_1_out));  // open: Q, clr
endmodule
