// Logisim project proyecto_circuito.circ as structural Verilog
module main (
);

  wire undriven, undriven_2;
  wire [1:0] undriven_3;
  wire [15:0] alu_1_resultado, banco_de_registros_1_busa, banco_de_registros_1_busb, bit_extender_1_out,
       multiplexer_1_out, register_1_q, rom_1_data;

  Register #(.width(16)) register_1 (.Q(register_1_q));  // open: D, en, clk, clr
  Adder #(.width(16)) adder_1 (.a(register_1_q), .b(16'h10));  // open: out, cin, cout
  ROM #(.dataWidth(16)) rom_1 (.addr(register_1_q[7:0]), .data(rom_1_data));
  assign bit_extender_1_out = {{12{rom_1_data[15]}}, rom_1_data[15:12]};  // Bit_Extender bit_extender_1
  Banco_de_registros banco_de_registros_1 (
    .regWR(undriven), .RA(rom_1_data[11:8]), .RW(rom_1_data[7:4]), .RB(rom_1_data[15:12]),
    .BusW(alu_1_resultado), .BusA(banco_de_registros_1_busa), .BusB(banco_de_registros_1_busb));
  Multiplexer #(.width(16)) multiplexer_1 (
    .in0(banco_de_registros_1_busb), .in1(bit_extender_1_out), .out(multiplexer_1_out), .sel(undriven_2));
  ALU alu_1 (
    .ALUop(undriven_3), .B(multiplexer_1_out), .A(banco_de_registros_1_busa), .resultado(alu_1_resultado));  // open: zero, negative, carry, overflow
endmodule

module Banco_de_registros (
  input  regWR,
  input  [3:0] RA,
  input  [3:0] RW,
  input  [3:0] RB,
  input  [15:0] BusW,
  output [15:0] BusA,
  output [15:0] BusB
);

  wire and_1_out, and_2_out, and_3_out, and_4_out, and_5_out, and_6_out, and_7_out, and_8_out, and_9_out,
       and_10_out, and_11_out, and_12_out, and_13_out, and_14_out, and_15_out, and_16_out, clock_1_out,
       decoder_1_out0, decoder_1_out1, decoder_1_out2, decoder_1_out3, decoder_1_out4, decoder_1_out5,
       decoder_1_out6, decoder_1_out7, decoder_1_out8, decoder_1_out9, decoder_1_out10, decoder_1_out11,
       decoder_1_out12, decoder_1_out13, decoder_1_out14, decoder_1_out15;
  wire [15:0] register_1_q, register_2_q, register_3_q, register_4_q, register_5_q, register_6_q,
       register_7_q, register_8_q, register_9_q, register_10_q, register_11_q, register_12_q, register_13_q,
       register_14_q, register_15_q, register_16_q;

  Decoder #(.enable("false"), .select(4)) decoder_1 (
    .out0(decoder_1_out0), .out1(decoder_1_out1), .out2(decoder_1_out2), .out3(decoder_1_out3),
    .out4(decoder_1_out4), .out5(decoder_1_out5), .out6(decoder_1_out6), .out7(decoder_1_out7),
    .out8(decoder_1_out8), .out9(decoder_1_out9), .out10(decoder_1_out10), .out11(decoder_1_out11),
    .out12(decoder_1_out12), .out13(decoder_1_out13), .out14(decoder_1_out14), .out15(decoder_1_out15),
    .sel(RW));
  and and_1 (and_1_out, regWR, decoder_1_out0);
  and and_2 (and_2_out, regWR, decoder_1_out1);
  and and_3 (and_3_out, regWR, decoder_1_out2);
  and and_4 (and_4_out, regWR, decoder_1_out3);
  and and_5 (and_5_out, regWR, decoder_1_out4);
  and and_6 (and_6_out, regWR, decoder_1_out5);
  and and_7 (and_7_out, regWR, decoder_1_out6);
  and and_8 (and_8_out, regWR, decoder_1_out7);
  and and_9 (and_9_out, regWR, decoder_1_out8);
  and and_10 (and_10_out, regWR, decoder_1_out9);
  and and_11 (and_11_out, regWR, decoder_1_out10);
  and and_12 (and_12_out, regWR, decoder_1_out11);
  and and_13 (and_13_out, regWR, decoder_1_out12);
  and and_14 (and_14_out, regWR, decoder_1_out13);
  and and_15 (and_15_out, regWR, decoder_1_out14);
  and and_16 (and_16_out, regWR, decoder_1_out15);
  Clock clock_1 (.out(clock_1_out));
  Register #(.width(16)) register_1 (.D(BusW), .en(and_1_out), .clk(clock_1_out), .Q(register_1_q));  // open: clr
  Register #(.width(16)) register_2 (.D(BusW), .en(and_2_out), .clk(clock_1_out), .Q(register_2_q));  // open: clr
  Register #(.width(16)) register_3 (.D(BusW), .en(and_3_out), .clk(clock_1_out), .Q(register_3_q));  // open: clr
  Register #(.width(16)) register_4 (.D(BusW), .en(and_4_out), .clk(clock_1_out), .Q(register_4_q));  // open: clr
  Register #(.width(16)) register_5 (.D(BusW), .en(and_5_out), .clk(clock_1_out), .Q(register_5_q));  // open: clr
  Register #(.width(16)) register_6 (.D(BusW), .en(and_6_out), .clk(clock_1_out), .Q(register_6_q));  // open: clr
  Register #(.width(16)) register_7 (.D(BusW), .en(and_7_out), .clk(clock_1_out), .Q(register_7_q));  // open: clr
  Register #(.width(16)) register_8 (.D(BusW), .en(and_8_out), .clk(clock_1_out), .Q(register_8_q));  // open: clr
  Register #(.width(16)) register_9 (.D(BusW), .en(and_9_out), .clk(clock_1_out), .Q(register_9_q));  // open: clr
  Register #(.width(16)) register_10 (.D(BusW), .en(and_10_out), .clk(clock_1_out), .Q(register_10_q));  // open: clr
  Register #(.width(16)) register_11 (.D(BusW), .en(and_11_out), .clk(clock_1_out), .Q(register_11_q));  // open: clr
  Register #(.width(16)) register_12 (.D(BusW), .en(and_12_out), .clk(clock_1_out), .Q(register_12_q));  // open: clr
  Register #(.width(16)) register_13 (.D(BusW), .en(and_13_out), .clk(clock_1_out), .Q(register_13_q));  // open: clr
  Register #(.width(16)) register_14 (.D(BusW), .en(and_14_out), .clk(clock_1_out), .Q(register_14_q));  // open: clr
  Register #(.width(16)) register_15 (.D(BusW), .en(and_15_out), .clk(clock_1_out), .Q(register_15_q));  // open: clr
  Register #(.width(16)) register_16 (.D(BusW), .en(and_16_out), .clk(clock_1_out), .Q(register_16_q));  // open: clr
  Multiplexer #(.select(4), .width(16)) multiplexer_1 (
    .in0(register_1_q), .in1(register_2_q), .in2(register_3_q), .in3(register_4_q), .in4(register_5_q),
    .in5(register_6_q), .in6(register_7_q), .in7(register_8_q), .in8(register_9_q), .in9(register_10_q),
    .in10(register_11_q), .in11(register_12_q), .in12(register_13_q), .in13(register_14_q),
    .in14(register_15_q), .in15(register_16_q), .out(BusA), .sel(RA));
  Multiplexer #(.select(4), .width(16)) multiplexer_2 (
    .in0(register_1_q), .in1(register_2_q), .in2(register_3_q), .in3(register_4_q), .in4(register_5_q),
    .in5(register_6_q), .in6(register_7_q), .in7(register_8_q), .in8(register_9_q), .in9(register_10_q),
    .in10(register_11_q), .in11(register_12_q), .in12(register_13_q), .in13(register_14_q),
    .in14(register_15_q), .in15(register_16_q), .out(BusB), .sel(RB));
endmodule

module ALU (
  input  [1:0] ALUop,
  input  [15:0] B,
  input  [15:0] A,
  output [15:0] resultado,
  output zero,
  output negative,
  output carry,
  output overflow
);

  wire adder_1_cout, not_2_out, xnor_1_out, xor_1_out;
  wire [14:0] adder_1_out;
  wire [15:0] multiplexer_1_out, not_1_out, not_3_out, O_out, Y_out;
  wire [15:15] adder_1_out_2;

  assign not_1_out = ~B;  // NOT_Gate not_1, 16 bits wide
  Multiplexer #(.width(16)) multiplexer_1 (.in0(B), .in1(not_1_out), .out(multiplexer_1_out), .sel(ALUop[0]));
  Adder #(.width(16)) adder_1 (
    .a(multiplexer_1_out), .b(A), .out({adder_1_out_2[15], adder_1_out}), .cin(ALUop[0]), .cout(adder_1_cout));
  not not_2 (not_2_out, ALUop[1]);
  assign Y_out = B & A;  // AND_Gate Y, 16 bits wide
  assign O_out = B | A;  // OR_Gate O, 16 bits wide
  xor xor_1 (xor_1_out, adder_1_out_2[15], A[15]);
  NotExactlyOne xnor_1 (.out(xnor_1_out), .in0(A[15]), .in1(ALUop[0]), .in2(B[15]));
  assign not_3_out = ~A;  // NOT_Gate not_3, 16 bits wide
  Multiplexer #(.select(3), .width(16)) multiplexer_2 (
    .in2({adder_1_out_2[15], adder_1_out}), .in3({adder_1_out_2[15], adder_1_out}), .in4(Y_out), .in5(O_out),
    .in6(not_3_out), .out({negative, resultado[14:0]}));  // open: in0, in1, in7, sel
  and and_1 (carry, adder_1_cout, not_2_out);
  and and_2 (overflow, not_2_out, xor_1_out, xnor_1_out);
  Comparator #(.width(16)) comparator_1 (.a({negative, resultado[14:0]}), .eq(zero));  // open: b, gt, lt

  assign resultado[15] = negative;
endmodule
