// Logisim project proyecto_final.circ as structural Verilog: 4 circuits, main circuit main
module main (
);

  wire alu_1_zero, and_1_out, clock_1_out, undriven, unidad_de_control1_1_alusrc,
       unidad_de_control1_1_branch, unidad_de_control1_1_mayorig, unidad_de_control1_1_memrd,
       unidad_de_control1_1_memtoreg, unidad_de_control1_1_memwr, unidad_de_control1_1_regwr;
  wire [2:0] unidad_de_control1_1_aluop;
  wire [7:0] alu_1_resultado;
  wire [15:0] adder_1_out, adder_2_out, banco_de_registros_1_busa, banco_de_registros_1_busb,
       banco_de_registros_1_busc, bit_extender_1_out, multiplexer_1_out, multiplexer_2_out,
       multiplexer_3_out, multiplexer_4_out, PC_q, ram_1_dout, rom_1_data;
  wire [15:8] alu_1_resultado_2;

  Register #(.width(16)) PC (.D(multiplexer_3_out), .clk(clock_1_out), .Q(PC_q), .clr(undriven));  // open: en
  Clock clock_1 (.out(clock_1_out));
  Adder #(.width(16)) adder_1 (.a(PC_q), .b(16'h1), .out(adder_1_out));  // open: cin, cout
  ROM #(.addrWidth(16), .dataWidth(16)) rom_1 (.addr(PC_q), .data(rom_1_data));
  Unidad_de_Control1 unidad_de_control1_1 (
    .opcode(rom_1_data[3:0]), .aluOP(unidad_de_control1_1_aluop), .ALUsrc(unidad_de_control1_1_alusrc),
    .MemtoReg(unidad_de_control1_1_memtoreg), .regWR(unidad_de_control1_1_regwr),
    .MemRD(unidad_de_control1_1_memrd), .MemWR(unidad_de_control1_1_memwr),
    .Branch(unidad_de_control1_1_branch), .MayorIg(unidad_de_control1_1_mayorig));
  Banco_de_registros banco_de_registros_1 (
    .RW(rom_1_data[7:4]), .RB(rom_1_data[15:12]), .RA(rom_1_data[11:8]), .regWR(unidad_de_control1_1_regwr),
    .BusW(multiplexer_4_out), .BusA(banco_de_registros_1_busa), .BusB(banco_de_registros_1_busb),
    .BusC(banco_de_registros_1_busc));
  assign bit_extender_1_out = {{12{rom_1_data[15]}}, rom_1_data[15:12]};  // Bit_Extender bit_extender_1
  Adder #(.width(16)) adder_2 (.a(PC_q), .b(bit_extender_1_out), .out(adder_2_out));  // open: cin, cout
  Multiplexer #(.width(16)) multiplexer_1 (
    .in0(banco_de_registros_1_busb), .in1(bit_extender_1_out), .out(multiplexer_1_out),
    .sel(unidad_de_control1_1_alusrc));
  Multiplexer #(.width(16)) multiplexer_2 (
    .in0(multiplexer_1_out), .in1(banco_de_registros_1_busc), .out(multiplexer_2_out),
    .sel(unidad_de_control1_1_branch));
  Multiplexer #(.width(16)) multiplexer_3 (
    .in0(adder_1_out), .in1(adder_2_out), .out(multiplexer_3_out), .sel(and_1_out));
  and and_1 (and_1_out, unidad_de_control1_1_branch, alu_1_zero);
  ALU alu_1 (
    .ALUop(unidad_de_control1_1_aluop), .B(multiplexer_2_out), .A(banco_de_registros_1_busa),
    .resultado({alu_1_resultado_2, alu_1_resultado}), .zero(alu_1_zero),
    .Mayorig(unidad_de_control1_1_mayorig));
  RAM #(.dataWidth(16)) ram_1 (
    .addr(alu_1_resultado), .we(unidad_de_control1_1_memwr), .oe(unidad_de_control1_1_memrd),
    .clk(clock_1_out), .din(banco_de_registros_1_busc), .dout(ram_1_dout));
  Multiplexer #(.width(16)) multiplexer_4 (
    .in0(ram_1_dout), .in1({alu_1_resultado_2, alu_1_resultado}), .out(multiplexer_4_out),
    .sel(unidad_de_control1_1_memtoreg));

  // Notes on the sheet:
  //   contents of rom_1 (hex, n*v repeats v):
  //   5446 45 5*1116 7418 6*0 4415
endmodule

module ALU (
  input  [2:0] ALUop,
  input  [15:0] B,
  input  [15:0] A,
  output [15:0] resultado,
  output zero,
  output Mayorig
);

  wire comparator_1_lt;
  wire [15:0] adder_1_out, multiplexer_1_out, not_1_out, not_2_out, O_out, Y_out;

  assign not_1_out = ~B;  // NOT_Gate not_1, 16 bits wide
  Multiplexer #(.width(16)) multiplexer_1 (.in0(B), .in1(not_1_out), .out(multiplexer_1_out), .sel(ALUop[0]));
  Adder #(.width(16)) adder_1 (.a(multiplexer_1_out), .b(A), .out(adder_1_out), .cin(ALUop[0]));  // open: cout
  assign Y_out = B & A;  // AND_Gate Y, 16 bits wide
  assign O_out = B | A;  // OR_Gate O, 16 bits wide
  assign not_2_out = ~A;  // NOT_Gate not_2, 16 bits wide
  Multiplexer #(.select(3), .width(16)) multiplexer_2 (
    .in0(adder_1_out), .in1(adder_1_out), .in2(Y_out), .in3(O_out), .in4(not_2_out), .out(resultado),
    .sel(ALUop));  // open: in5, in6, in7
  Comparator #(.width(16)) comparator_1 (.a(resultado), .b({16{1'b0}}), .eq(zero), .lt(comparator_1_lt));  // open: gt
  not not_3 (Mayorig, comparator_1_lt);
endmodule

module Banco_de_registros (
  input  regWR,
  input  [3:0] RA,
  input  [3:0] RW,
  input  [3:0] RB,
  input  [15:0] BusW,
  output [15:0] BusA,
  output [15:0] BusB,
  output [15:0] BusC
);

  wire and_1_out, and_2_out, and_3_out, and_4_out, and_5_out, and_6_out, and_7_out, and_8_out, and_9_out,
       and_10_out, and_11_out, and_12_out, and_13_out, and_14_out, and_15_out, and_16_out, clock_1_out,
       demultiplexer_1_out0, demultiplexer_1_out1, demultiplexer_1_out2, demultiplexer_1_out3,
       demultiplexer_1_out4, demultiplexer_1_out5, demultiplexer_1_out6, demultiplexer_1_out7,
       demultiplexer_1_out8, demultiplexer_1_out9, demultiplexer_1_out10, demultiplexer_1_out11,
       demultiplexer_1_out12, demultiplexer_1_out13, demultiplexer_1_out14, demultiplexer_1_out15;
  wire [15:0] x0_q, xa_q, xb_q, xc_q, xd_q, xe_q, xf_q, xg_q, xh_q, xi_q, xj_q, xk_q, xl_q, xm_q, xn_q, xw_q;

  Demultiplexer #(.select(4)) demultiplexer_1 (
    .out0(demultiplexer_1_out0), .out1(demultiplexer_1_out1), .out2(demultiplexer_1_out2),
    .out3(demultiplexer_1_out3), .out4(demultiplexer_1_out4), .out5(demultiplexer_1_out5),
    .out6(demultiplexer_1_out6), .out7(demultiplexer_1_out7), .out8(demultiplexer_1_out8),
    .out9(demultiplexer_1_out9), .out10(demultiplexer_1_out10), .out11(demultiplexer_1_out11),
    .out12(demultiplexer_1_out12), .out13(demultiplexer_1_out13), .out14(demultiplexer_1_out14),
    .out15(demultiplexer_1_out15), .sel(RW));  // open: in
  and and_1 (and_1_out, regWR, demultiplexer_1_out0);
  and and_2 (and_2_out, regWR, demultiplexer_1_out1);
  and and_3 (and_3_out, regWR, demultiplexer_1_out2);
  and and_4 (and_4_out, regWR, demultiplexer_1_out3);
  and and_5 (and_5_out, regWR, demultiplexer_1_out4);
  and and_6 (and_6_out, regWR, demultiplexer_1_out5);
  and and_7 (and_7_out, regWR, demultiplexer_1_out6);
  and and_8 (and_8_out, regWR, demultiplexer_1_out7);
  and and_9 (and_9_out, regWR, demultiplexer_1_out8);
  and and_10 (and_10_out, regWR, demultiplexer_1_out9);
  and and_11 (and_11_out, regWR, demultiplexer_1_out10);
  and and_12 (and_12_out, regWR, demultiplexer_1_out11);
  and and_13 (and_13_out, regWR, demultiplexer_1_out12);
  and and_14 (and_14_out, regWR, demultiplexer_1_out13);
  and and_15 (and_15_out, regWR, demultiplexer_1_out14);
  and and_16 (and_16_out, regWR, demultiplexer_1_out15);
  Clock clock_1 (.out(clock_1_out));
  Register #(.width(16)) x0 (.D(BusW), .en(and_1_out), .clk(clock_1_out), .Q(x0_q));  // open: clr
  Register #(.width(16)) xa (.D(BusW), .en(and_2_out), .clk(clock_1_out), .Q(xa_q));  // open: clr
  Register #(.width(16)) xb (.D(BusW), .en(and_3_out), .clk(clock_1_out), .Q(xb_q));  // open: clr
  Register #(.width(16)) xc (.D(BusW), .en(and_4_out), .clk(clock_1_out), .Q(xc_q));  // open: clr
  Register #(.width(16)) xd (.D(BusW), .en(and_5_out), .clk(clock_1_out), .Q(xd_q));  // open: clr
  Register #(.width(16)) xe (.D(BusW), .en(and_6_out), .clk(clock_1_out), .Q(xe_q));  // open: clr
  Register #(.width(16)) xf (.D(BusW), .en(and_7_out), .clk(clock_1_out), .Q(xf_q));  // open: clr
  Register #(.width(16)) xg (.D(BusW), .en(and_8_out), .clk(clock_1_out), .Q(xg_q));  // open: clr
  Register #(.width(16)) xh (.D(BusW), .en(and_9_out), .clk(clock_1_out), .Q(xh_q));  // open: clr
  Register #(.width(16)) xi (.D(BusW), .en(and_10_out), .clk(clock_1_out), .Q(xi_q));  // open: clr
  Register #(.width(16)) xj (.D(BusW), .en(and_11_out), .clk(clock_1_out), .Q(xj_q));  // open: clr
  Register #(.width(16)) xk (.D(BusW), .en(and_12_out), .clk(clock_1_out), .Q(xk_q));  // open: clr
  Register #(.width(16)) xl (.D(BusW), .en(and_13_out), .clk(clock_1_out), .Q(xl_q));  // open: clr
  Register #(.width(16)) xm (.D(BusW), .en(and_14_out), .clk(clock_1_out), .Q(xm_q));  // open: clr
  Register #(.width(16)) xn (.D(BusW), .en(and_15_out), .clk(clock_1_out), .Q(xn_q));  // open: clr
  Register #(.width(16)) xw (.D(BusW), .en(and_16_out), .clk(clock_1_out), .Q(xw_q));  // open: clr
  Multiplexer #(.select(4), .width(16)) multiplexer_1 (
    .in0(x0_q), .in1(xa_q), .in2(xb_q), .in3(xc_q), .in4(xd_q), .in5(xe_q), .in6(xf_q), .in7(xg_q),
    .in8(xh_q), .in9(xi_q), .in10(xj_q), .in11(xk_q), .in12(xl_q), .in13(xm_q), .in14(xn_q), .in15(xw_q),
    .out(BusA), .sel(RA));
  Multiplexer #(.select(4), .width(16)) multiplexer_2 (
    .in0(x0_q), .in1(xa_q), .in2(xb_q), .in3(xc_q), .in4(xd_q), .in5(xe_q), .in6(xf_q), .in7(xg_q),
    .in8(xh_q), .in9(xi_q), .in10(xj_q), .in11(xk_q), .in12(xl_q), .in13(xm_q), .in14(xn_q), .in15(xw_q),
    .out(BusB), .sel(RB));
  Multiplexer #(.select(4), .width(16)) multiplexer_3 (
    .in0(x0_q), .in1(xa_q), .in2(xb_q), .in3(xc_q), .in4(xd_q), .in5(xe_q), .in6(xf_q), .in7(xg_q),
    .in8(xh_q), .in9(xi_q), .in10(xj_q), .in11(xk_q), .in12(xl_q), .in13(xm_q), .in14(xn_q), .in15(xw_q),
    .out(BusC), .sel(RW));
endmodule

module Unidad_de_Control1 (
  input  [3:0] opcode,
  output [2:0] aluOP,
  output ALUsrc,
  output MemtoReg,
  output regWR,
  output MemRD,
  output MemWR,
  output Branch,
  output MayorIg
);

  wire and_3_out, and_4_out, and_5_out, and_6_out, and_7_out, and_8_out, and_9_out, and_10_out, not_1_out,
       not_2_out, not_3_out, not_4_out;

  not not_1 (not_1_out, opcode[3]);
  not not_2 (not_2_out, opcode[2]);
  not not_3 (not_3_out, opcode[1]);
  not not_4 (not_4_out, opcode[0]);
  and and_1 (aluOP[2], opcode[2], opcode[1], opcode[0]);
  and and_2 (aluOP[1], not_2_out, opcode[1]);
  and and_3 (and_3_out, not_2_out, opcode[0]);
  and and_4 (and_4_out, opcode[2], opcode[1], not_4_out);
  and and_5 (and_5_out, opcode[3], opcode[1], opcode[0]);
  and and_6 (and_6_out, opcode[3], opcode[2]);
  and and_7 (and_7_out, not_1_out, opcode[2], not_3_out);
  and and_8 (and_8_out, opcode[2], not_3_out, not_4_out);
  and and_9 (and_9_out, not_1_out, not_2_out);
  and and_10 (and_10_out, not_1_out, not_4_out);
  and and_11 (MemRD, opcode[2], not_3_out, not_4_out);
  and and_12 (MemWR, opcode[2], not_3_out, opcode[0]);
  and and_13 (MayorIg, opcode[3], not_2_out, opcode[1], not_4_out);
  or or_1 (aluOP[0], and_3_out, opcode[3]);
  or or_2 (ALUsrc, and_4_out, and_5_out, and_6_out);
  nor nor_1 (MemtoReg, and_7_out, and_8_out);
  or or_3 (regWR, and_9_out, and_10_out, opcode[1]);

  assign Branch = opcode[3];
endmodule
