// Logisim project proyecto_final_3mesa.circ as structural Verilog: 5 circuits, main circuit main
module main (
);

  wire alu_1_mayor, alu_1_zero, and_1_out, and_2_out, clock_1_out, or_1_out, or_2_out,
       unidad_de_control_1_alusrc, unidad_de_control_1_igual, unidad_de_control_1_mayor,
       unidad_de_control_1_memtoreg, unidad_de_control_1_memwr, unidad_de_control_1_regwr,
       unidad_de_control_1_resta;
  wire [2:0] unidad_de_control_1_aluop;
  wire [7:0] alu_1_resultado, banco_de_registros_1_busc, banco_de_registros_1_busc_2, ram_1_p8, ram_1_p9,
       rom_1_p1, rom_1_p3, rom_1_p4;
  wire [15:0] adder_1_out, adder_2_out, banco_de_registros_1_busa, banco_de_registros_1_busb,
       extensor_de_signo_1_out_3, multiplexer_1_out, multiplexer_2_out, multiplexer_3_out, multiplexer_4_out,
       PC_q;
  wire [15:8] alu_1_resultado_2;

  Clock clock_1 (.out(clock_1_out));
  Register #(.width(16)) PC (.D(multiplexer_3_out), .clk(clock_1_out), .Q(PC_q));  // open: en, clr
  Adder #(.width(16)) adder_1 (.a(PC_q), .b(16'h2), .out(adder_1_out));  // open: cin, cout
  // ROM #(.line("dual")) rom_1: pin names not known; wires that end beside it: rom_1_p1, adder_1_out, rom_1_p3, rom_1_p4
  Bit_Extender #(.in_width(16), .out_width(8)) bit_extender_1 (.in(PC_q), .out(rom_1_p1));
  Unidad_de_Control unidad_de_control_1 (
    .opcode(rom_1_p3[3:0]), .aluOP(unidad_de_control_1_aluop), .ALUsrc(unidad_de_control_1_alusrc),
    .MemtoReg(unidad_de_control_1_memtoreg), .regWR(unidad_de_control_1_regwr),
    .resta(unidad_de_control_1_resta), .MemWR(unidad_de_control_1_memwr), .igual(unidad_de_control_1_igual),
    .mayor(unidad_de_control_1_mayor));
  Banco_de_registros banco_de_registros_1 (
    .RW(rom_1_p3[7:4]), .RB(rom_1_p4[7:4]), .RA(rom_1_p4[3:0]), .regWR(unidad_de_control_1_regwr),
    .BusW(multiplexer_4_out), .BusA(banco_de_registros_1_busa), .BusB(banco_de_registros_1_busb),
    .BusC({banco_de_registros_1_busc_2, banco_de_registros_1_busc}));
  extensor_de_signo extensor_de_signo_1 (
    .in_1(unidad_de_control_1_resta), .in_2(rom_1_p4[7:4]), .out_3(extensor_de_signo_1_out_3));
  Adder #(.width(16)) adder_2 (.a(PC_q), .b(extensor_de_signo_1_out_3), .out(adder_2_out));  // open: cin, cout
  Multiplexer #(.width(16)) multiplexer_1 (
    .in0(banco_de_registros_1_busb), .in1(extensor_de_signo_1_out_3), .out(multiplexer_1_out),
    .sel(unidad_de_control_1_alusrc));
  or or_1 (or_1_out, unidad_de_control_1_mayor, unidad_de_control_1_igual);
  Multiplexer #(.width(16)) multiplexer_2 (
    .in0(multiplexer_1_out), .in1({banco_de_registros_1_busc_2, banco_de_registros_1_busc}),
    .out(multiplexer_2_out), .sel(or_1_out));
  Multiplexer #(.width(16)) multiplexer_3 (
    .in0(adder_1_out), .in1(adder_2_out), .out(multiplexer_3_out), .sel(or_2_out));
  ALU alu_1 (
    .ALUop(unidad_de_control_1_aluop), .B(multiplexer_2_out), .A(banco_de_registros_1_busa),
    .resultado({alu_1_resultado_2, alu_1_resultado}), .Mayor(alu_1_mayor), .zero(alu_1_zero));
  and and_1 (and_1_out, unidad_de_control_1_igual, alu_1_zero);
  and and_2 (and_2_out, unidad_de_control_1_mayor, alu_1_mayor);
  or or_2 (or_2_out, and_1_out, and_2_out);
  // RAM #(.enables("line"), .line("dual")) ram_1: pin names not known; wires that end beside it: alu_1_resultado, unidad_de_control_1_memwr, unidad_de_control_1_memwr, unidad_de_control_1_memwr, clock_1_out, banco_de_registros_1_busc, banco_de_registros_1_busc_2, ram_1_p8, ram_1_p9
  Multiplexer #(.width(16)) multiplexer_4 (
    .in0({ram_1_p9, ram_1_p8}), .in1({alu_1_resultado_2, alu_1_resultado}), .out(multiplexer_4_out),
    .sel(unidad_de_control_1_memtoreg));

  // Notes on the sheet:
  //   contents of rom_1 (hex, n*v repeats v):
  //   16 80 26 a0 94 1 a4 2 98 aa 25 0 98 a9 4*0 5 10 5 20
  //   aaaaaaaaaa
endmodule

module ALU (
  input  [2:0] ALUop,
  input  [15:0] B,
  input  [15:0] A,
  output [15:0] resultado,
  output Mayor,
  output zero
);

  wire [15:0] adder_1_out, multiplexer_1_out, not_1_out, not_2_out, O_out, Y_out;

  assign not_1_out = ~B;  // NOT_Gate not_1, 16 bits wide
  Multiplexer #(.width(16)) multiplexer_1 (.in0(B), .in1(not_1_out), .out(multiplexer_1_out), .sel(ALUop[0]));
  Adder #(.width(16)) adder_1 (.a(multiplexer_1_out), .b(A), .out(adder_1_out), .cin(ALUop[0]));  // open: cout
  assign Y_out = B & A;  // AND_Gate Y, 16 bits wide
  assign O_out = B | A;  // OR_Gate O, 16 bits wide
  assign not_2_out = ~A;  // NOT_Gate not_2, 16 bits wide
  Multiplexer #(.select(3), .width(16)) multiplexer_2 (
    .in0(adder_1_out), .in1(adder_1_out), .in2(Y_out), .in3(O_out), .in4(not_2_out), .out(resultado),
    .sel(ALUop));  // open: in5, in6, in7
  Comparator #(.width(16)) comparator_1 (.a(resultado), .b({16{1'b0}}), .gt(Mayor), .eq(zero));  // open: lt
endmodule

module Banco_de_registros (
  input  regWR,
  input  [3:0] RA,
  input  [3:0] RW,
  input  [3:0] RB,
  input  [15:0] BusW,
  output [15:0] BusA,
  output [15:0] BusB,
  output [15:0] BusC
);

  wire and_1_out, and_2_out, and_3_out, and_4_out, and_5_out, and_6_out, and_7_out, and_8_out, and_9_out,
       and_10_out, and_11_out, and_12_out, and_13_out, and_14_out, and_15_out, and_16_out, clock_1_out,
       demultiplexer_1_out0, demultiplexer_1_out1, demultiplexer_1_out2, demultiplexer_1_out3,
       demultiplexer_1_out4, demultiplexer_1_out5, demultiplexer_1_out6, demultiplexer_1_out7,
       demultiplexer_1_out8, demultiplexer_1_out9, demultiplexer_1_out10, demultiplexer_1_out11,
       demultiplexer_1_out12, demultiplexer_1_out13, demultiplexer_1_out14, demultiplexer_1_out15;
  wire [15:0] x0_q, xa_q, xb_q, xc_q, xd_q, xe_q, xf_q, xg_q, xh_q, xi_q, xj_q, xk_q, xl_q, xm_q, xn_q, xw_q;

  Demultiplexer #(.select(4)) demultiplexer_1 (
    .out0(demultiplexer_1_out0), .out1(demultiplexer_1_out1), .out2(demultiplexer_1_out2),
    .out3(demultiplexer_1_out3), .out4(demultiplexer_1_out4), .out5(demultiplexer_1_out5),
    .out6(demultiplexer_1_out6), .out7(demultiplexer_1_out7), .out8(demultiplexer_1_out8),
    .out9(demultiplexer_1_out9), .out10(demultiplexer_1_out10), .out11(demultiplexer_1_out11),
    .out12(demultiplexer_1_out12), .out13(demultiplexer_1_out13), .out14(demultiplexer_1_out14),
    .out15(demultiplexer_1_out15), .sel(RW));  // open: in
  and and_1 (and_1_out, regWR, demultiplexer_1_out0);
  and and_2 (and_2_out, regWR, demultiplexer_1_out1);
  and and_3 (and_3_out, regWR, demultiplexer_1_out2);
  and and_4 (and_4_out, regWR, demultiplexer_1_out3);
  and and_5 (and_5_out, regWR, demultiplexer_1_out4);
  and and_6 (and_6_out, regWR, demultiplexer_1_out5);
  and and_7 (and_7_out, regWR, demultiplexer_1_out6);
  and and_8 (and_8_out, regWR, demultiplexer_1_out7);
  and and_9 (and_9_out, regWR, demultiplexer_1_out8);
  and and_10 (and_10_out, regWR, demultiplexer_1_out9);
  and and_11 (and_11_out, regWR, demultiplexer_1_out10);
  and and_12 (and_12_out, regWR, demultiplexer_1_out11);
  and and_13 (and_13_out, regWR, demultiplexer_1_out12);
  and and_14 (and_14_out, regWR, demultiplexer_1_out13);
  and and_15 (and_15_out, regWR, demultiplexer_1_out14);
  and and_16 (and_16_out, regWR, demultiplexer_1_out15);
  Clock clock_1 (.out(clock_1_out));
  Register #(.width(16)) x0 (.D(BusW), .en(and_1_out), .clk(clock_1_out), .Q(x0_q));  // open: clr
  Register #(.width(16)) xa (.D(BusW), .en(and_2_out), .clk(clock_1_out), .Q(xa_q));  // open: clr
  Register #(.width(16)) xb (.D(BusW), .en(and_3_out), .clk(clock_1_out), .Q(xb_q));  // open: clr
  Register #(.width(16)) xc (.D(BusW), .en(and_4_out), .clk(clock_1_out), .Q(xc_q));  // open: clr
  Register #(.width(16)) xd (.D(BusW), .en(and_5_out), .clk(clock_1_out), .Q(xd_q));  // open: clr
  Register #(.width(16)) xe (.D(BusW), .en(and_6_out), .clk(clock_1_out), .Q(xe_q));  // open: clr
  Register #(.width(16)) xf (.D(BusW), .en(and_7_out), .clk(clock_1_out), .Q(xf_q));  // open: clr
  Register #(.width(16)) xg (.D(BusW), .en(and_8_out), .clk(clock_1_out), .Q(xg_q));  // open: clr
  Register #(.width(16)) xh (.D(BusW), .en(and_9_out), .clk(clock_1_out), .Q(xh_q));  // open: clr
  Register #(.width(16)) xi (.D(BusW), .en(and_10_out), .clk(clock_1_out), .Q(xi_q));  // open: clr
  Register #(.width(16)) xj (.D(BusW), .en(and_11_out), .clk(clock_1_out), .Q(xj_q));  // open: clr
  Register #(.width(16)) xk (.D(BusW), .en(and_12_out), .clk(clock_1_out), .Q(xk_q));  // open: clr
  Register #(.width(16)) xl (.D(BusW), .en(and_13_out), .clk(clock_1_out), .Q(xl_q));  // open: clr
  Register #(.width(16)) xm (.D(BusW), .en(and_14_out), .clk(clock_1_out), .Q(xm_q));  // open: clr
  Register #(.width(16)) xn (.D(BusW), .en(and_15_out), .clk(clock_1_out), .Q(xn_q));  // open: clr
  Register #(.width(16)) xw (.D(BusW), .en(and_16_out), .clk(clock_1_out), .Q(xw_q));  // open: clr
  Multiplexer #(.select(4), .width(16)) multiplexer_1 (
    .in0(x0_q), .in1(xa_q), .in2(xb_q), .in3(xc_q), .in4(xd_q), .in5(xe_q), .in6(xf_q), .in7(xg_q),
    .in8(xh_q), .in9(xi_q), .in10(xj_q), .in11(xk_q), .in12(xl_q), .in13(xm_q), .in14(xn_q), .in15(xw_q),
    .out(BusA), .sel(RA));
  Multiplexer #(.select(4), .width(16)) multiplexer_2 (
    .in0(x0_q), .in1(xa_q), .in2(xb_q), .in3(xc_q), .in4(xd_q), .in5(xe_q), .in6(xf_q), .in7(xg_q),
    .in8(xh_q), .in9(xi_q), .in10(xj_q), .in11(xk_q), .in12(xl_q), .in13(xm_q), .in14(xn_q), .in15(xw_q),
    .out(BusB), .sel(RB));
  Multiplexer #(.select(4), .width(16)) multiplexer_3 (
    .in0(x0_q), .in1(xa_q), .in2(xb_q), .in3(xc_q), .in4(xd_q), .in5(xe_q), .in6(xf_q), .in7(xg_q),
    .in8(xh_q), .in9(xi_q), .in10(xj_q), .in11(xk_q), .in12(xl_q), .in13(xm_q), .in14(xn_q), .in15(xw_q),
    .out(BusC), .sel(RW));
endmodule

module Unidad_de_Control (
  input  [3:0] opcode,
  output [2:0] aluOP,
  output ALUsrc,
  output MemtoReg,
  output regWR,
  output resta,
  output MemWR,
  output igual,
  output mayor
);

  wire and_3_out, and_4_out, and_5_out, and_6_out, and_7_out, and_8_out, and_9_out, and_10_out, and_14_out,
       and_15_out, not_1_out, not_2_out, not_3_out, not_4_out;

  not not_1 (not_1_out, opcode[3]);
  not not_2 (not_2_out, opcode[2]);
  not not_3 (not_3_out, opcode[1]);
  not not_4 (not_4_out, opcode[0]);
  and and_1 (aluOP[2], opcode[2], opcode[1], opcode[0]);
  and and_2 (aluOP[1], not_2_out, opcode[1]);
  and and_3 (and_3_out, not_2_out, opcode[0]);
  and and_4 (and_4_out, opcode[2], opcode[1], not_4_out);
  and and_5 (and_5_out, opcode[3], opcode[1], opcode[0]);
  and and_6 (and_6_out, opcode[3], opcode[2]);
  and and_7 (and_7_out, not_1_out, opcode[2], not_3_out);
  and and_8 (and_8_out, opcode[2], not_3_out, not_4_out);
  and and_9 (and_9_out, not_1_out, not_2_out);
  and and_10 (and_10_out, not_1_out, not_4_out);
  and and_11 (resta, not_1_out, not_2_out, not_3_out, opcode[0]);
  and and_12 (MemWR, opcode[2], not_3_out, opcode[0]);
  and and_13 (igual, opcode[3], not_2_out, not_4_out);
  and and_14 (and_14_out, opcode[3], not_2_out, not_3_out, opcode[0]);
  and and_15 (and_15_out, opcode[3], not_2_out, opcode[1], not_4_out);
  or or_1 (aluOP[0], and_3_out, opcode[3]);
  or or_2 (ALUsrc, and_4_out, and_5_out, and_6_out);
  nor nor_1 (MemtoReg, and_7_out, and_8_out);
  or or_3 (regWR, and_9_out, and_10_out, opcode[1]);
  or or_4 (mayor, and_14_out, and_15_out);
endmodule

module extensor_de_signo (
  input  in_1,
  input  [3:0] in_2,
  output [15:0] out_3
);

  wire [15:0] bit_extender_1_out, bit_extender_2_out;

  assign bit_extender_1_out = {{12{1'b0}}, in_2};  // Bit_Extender bit_extender_1
  assign bit_extender_2_out = {{12{1'b1}}, in_2};  // Bit_Extender bit_extender_2
  Multiplexer #(.width(16)) multiplexer_1 (.in0(bit_extender_1_out), .in1(bit_extender_2_out), .out(out_3), .sel(in_1));
endmodule
